# Fritzing sketch MiniCalculator (saved by Fritzing 0.9.3b)
breadboards: 1

parts:
  Part1 = Arduino Uno (Rev3)
  R1 = Resistor [tolerance=±5% resistance=220 package=THT]
  R2 = Resistor [tolerance=±5% resistance=220 package=THT]
  R3 = Resistor [tolerance=±5% resistance=220 package=THT]
  R4 = Resistor [tolerance=±5% resistance=220 package=THT]
  R5 = Resistor [tolerance=±5% resistance=220 package=THT]
  R6 = Resistor [tolerance=±5% resistance=220 package=THT]
  R7 = Resistor [tolerance=±5% resistance=220 package=THT]
  7_Segment1 = 7 Segment Display
  7_Segment2 = 7 Segment Display
  7_Segment3 = 7 Segment Display
  7_Segment4 = 7 Segment Display
  Q1 = NPN-Transistor [part_number=BC337 package="TO92 [THT]"]
  Q2 = NPN-Transistor [part_number=BC337 package="TO92 [THT]"]
  Q3 = NPN-Transistor [part_number=BC337 package="TO92 [THT]"]
  Q4 = NPN-Transistor [part_number=BC337 package="TO92 [THT]"]
  S1 = Momentary Switch [part_number="[1]" package=ksa_sealed_tac_switch]
  S2 = Momentary Switch [part_number="[2]" package=ksa_sealed_tac_switch]
  S3 = Momentary Switch [part_number="[4]" package=ksa_sealed_tac_switch]
  S4 = Momentary Switch [part_number="[1]" package=ksa_sealed_tac_switch]
  S5 = Momentary Switch [part_number="[5]" package=ksa_sealed_tac_switch]
  S6 = Momentary Switch [part_number="[7]" package=ksa_sealed_tac_switch]
  S7 = Momentary Switch [part_number="[#]" package=ksa_sealed_tac_switch]
  S8 = Momentary Switch [part_number="[1]" package=ksa_sealed_tac_switch]
  S9 = Momentary Switch [part_number="[0]" package=ksa_sealed_tac_switch]
  S10 = Momentary Switch [part_number="[9]" package=ksa_sealed_tac_switch]
  S11 = Momentary Switch [part_number="[*]" package=ksa_sealed_tac_switch]
  S12 = Momentary Switch [part_number="[8]" package=ksa_sealed_tac_switch]

nets:
  N1: Part1.A0, S1.4, S2.4, S3.4
  N2: Part1.A1, S4.4, S5.4, S6.4
  N3: Part1.A2, S8.4, S10.4, S12.4
  N4: Part1.A3, S7.4, S9.4, S11.4
  N5: Part1.D8, R5.Pin_0
  N6: Part1.D9_PWM, Q1.B
  N7: Part1.D10_PWM/SS, Q2.B
  N8: Part1.D11_PWM/MOSI, Q3.B
  N9: Part1.D12/MISO, Q4.B
  N10: Part1.D13/SCK, S1.2, S4.2, S8.2, S11.2
  N11: Part1.A4/SDA, S3.2, S6.2, S7.2, S10.2
  N12: Part1.A5/SCL, S2.2, S5.2, S9.2, S12.2
  N13: Part1.D2, R6.Pin_0
  N14: Part1.D3_PWM, R7.Pin_0
  N15: Part1.D4, R1.Pin_0
  N16: Part1.D5_PWM, R2.Pin_0
  N17: Part1.D6_PWM, R3.Pin_0
  N18: Part1.D7, R4.Pin_0
  N19: R1.Pin_1, 7_Segment1.Segment_A, 7_Segment2.Segment_A, 7_Segment3.Segment_A, 7_Segment4.Segment_A
  N20: R2.Pin_1, 7_Segment1.Segment_B, 7_Segment2.Segment_B, 7_Segment3.Segment_B, 7_Segment4.Segment_B
  N21: R3.Pin_1, 7_Segment1.Segment_C, 7_Segment2.Segment_C, 7_Segment3.Segment_C, 7_Segment4.Segment_C
  N22: R4.Pin_1, 7_Segment1.Segment_D, 7_Segment2.Segment_D, 7_Segment3.Segment_D, 7_Segment4.Segment_D
  N23: R5.Pin_1, 7_Segment1.Segment_E, 7_Segment2.Segment_E, 7_Segment3.Segment_E, 7_Segment4.Segment_E
  N24: R6.Pin_1, 7_Segment1.Segment_F, 7_Segment2.Segment_F, 7_Segment3.Segment_F, 7_Segment4.Segment_F
  N25: R7.Pin_1, 7_Segment1.Segment_G, 7_Segment2.Segment_G, 7_Segment3.Segment_G, 7_Segment4.Segment_G
  N26: 7_Segment1.common_cathode, Q1.C
  N27: 7_Segment2.common_cathode, Q2.C
  N28: 7_Segment3.common_cathode, Q3.C
  N29: 7_Segment4.common_cathode, Q4.C
  GND: Q1.E, Q2.E, Q3.E, Q4.E
